// Logisim project Proyecto_flip_flop.circ as structural Verilog: 1 circuit, main circuit main
module main (
  input  in_1
);

  wire and_1_out, and_2_out, and_3_out, and_4_out, and_5_out, and_6_out, clock_1_out, d_ff_1_q, d_ff_2_q,
       d_ff_3_q, not_1_out, not_2_out, not_3_out, not_4_out, or_1_out, or_2_out, or_3_out;

  Clock clock_1 (.out(clock_1_out));
  D_Flip_Flop d_ff_1 (.D(or_3_out), .clk(clock_1_out), .Q(d_ff_1_q));  // open: Qn, preset, reset
  D_Flip_Flop d_ff_2 (.D(or_2_out), .clk(clock_1_out), .Q(d_ff_2_q));  // open: Qn, preset, reset
  D_Flip_Flop d_ff_3 (.D(or_1_out), .clk(clock_1_out), .Q(d_ff_3_q));  // open: Qn, preset, reset
  not not_1 (not_1_out, d_ff_1_q);
  LED led_1 (.in(d_ff_1_q));
  not not_2 (not_2_out, d_ff_2_q);
  LED led_2 (.in(d_ff_2_q));
  not not_3 (not_3_out, d_ff_3_q);
  LED led_3 (.in(d_ff_3_q));
  not not_4 (not_4_out, in_1);
  and and_1 (and_1_out, not_1_out, not_3_out);
  or or_1 (or_1_out, and_1_out, in_1);
  and and_2 (and_2_out, not_1_out, not_2_out, d_ff_3_q, not_4_out);
  and and_3 (and_3_out, not_1_out, d_ff_2_q, not_3_out, in_1);
  or or_2 (or_2_out, and_2_out, and_3_out);
  and and_4 (and_4_out, not_1_out, not_3_out, not_4_out);
  and and_5 (and_5_out, not_1_out, d_ff_3_q, in_1);
  and and_6 (and_6_out, not_1_out, d_ff_2_q, d_ff_3_q, not_4_out);
  or or_3 (or_3_out, and_4_out, and_5_out, and_6_out);
endmodule
